// Logisim project hw1q2 (complicated).circ as structural Verilog: 1 circuit, main circuit main
module main (
  input  X2,
  input  X1,
  input  X0,
  input  Y2,
  input  Y1,
  input  Y0,
  input  X2_2,
  input  X1_2,
  input  X0_2,
  input  Y2_2,
  input  Y1_2,
  input  Y0_2,
  output out_13,
  output out_14
);

  wire _0_2_out, _0_out, and_1_out, and_2_out, and_3_out, and_4_out, not_1_out, not_2_out, not_3_out,
       not_4_out, not_5_out, not_6_out, not_7_out, not_8_out, not_9_out, not_10_out, not_11_out, not_12_out;

  not not_1 (not_1_out, X2);
  not not_2 (not_2_out, X1);
  not not_3 (not_3_out, X0);
  not not_4 (not_4_out, Y2);
  not not_5 (not_5_out, Y1);
  not not_6 (not_6_out, Y0);
  not not_7 (not_7_out, X0_2);
  not not_8 (not_8_out, Y0_2);
  and _0 (_0_out, not_1_out, not_2_out, not_3_out);
  and _0_2 (_0_2_out, not_4_out, not_5_out, not_6_out);
  not not_9 (not_9_out, _0_out);
  not not_10 (not_10_out, _0_2_out);
  not not_11 (not_11_out, not_7_out);
  not not_12 (not_12_out, not_8_out);
  and and_1 (and_1_out, not_9_out, not_10_out);
  and and_2 (and_2_out, _0_out, _0_2_out);
  and and_3 (and_3_out, not_11_out, not_12_out);
  and and_4 (and_4_out, not_7_out, not_8_out);
  or or_1 (out_13, and_1_out, and_2_out);
  or or_2 (out_14, and_3_out, and_4_out);
endmodule
