// Logisim project ALU.circ as structural Verilog: 3 circuits, main circuit main
module main (
  input  [3:0] zx,
  input  [3:0] nx,
  input  [3:0] zy,
  input  [3:0] ny,
  input  [3:0] f,
  input  [3:0] no,
  input  [3:0] x,
  input  [3:0] x_0,
  input  [3:0] y,
  input  [3:0] y_0,
  output [3:0] \output ,
  output out_12
);

  wire [3:0] adder_1_out, And_out, flipper_1_out, flipper_2_out, flipper_3_out, mux2_1_out, mux2_2_out,
       mux2_3_out, mux2_4_out, mux2_5_out;

  mux2 mux2_1 (.select(zx), .line0(x), .line1(x_0), .out(mux2_1_out));
  mux2 mux2_2 (.select(nx), .line0(mux2_1_out), .line1(flipper_1_out), .out(mux2_2_out));
  flipper flipper_1 (.in(mux2_1_out), .out(flipper_1_out));
  mux2 mux2_3 (.select(zy), .line0(y), .line1(y_0), .out(mux2_3_out));
  flipper flipper_2 (.in(mux2_3_out), .out(flipper_2_out));
  mux2 mux2_4 (.select(ny), .line0(mux2_3_out), .line1(flipper_2_out), .out(mux2_4_out));
  assign And_out = mux2_2_out & mux2_4_out;  // AND_Gate And, 4 bits wide
  Adder #(.width(4)) adder_1 (.a(mux2_2_out), .b(mux2_4_out), .out(adder_1_out), .cout(out_12));  // open: cin
  mux2 mux2_5 (.select(f), .line0(And_out), .line1(adder_1_out), .out(mux2_5_out));
  flipper flipper_3 (.in(mux2_5_out), .out(flipper_3_out));
  mux2 mux2_6 (.select(no), .line0(mux2_5_out), .line1(flipper_3_out), .out(\output ));

  // Notes on the sheet:
  //   x calculations
  //   y calculations
  //   My (Keith Ng) attempt at the ALU, with 4-bit wide inputs and gates (4-bit wide stuff was a lot easier than I expected)
  //   And or Add?
  //   This output signifies
  //   that the addition
  //   carried out of range!
  //   Using the flipper again to
  //   invert number if no is on
endmodule

// mux
module mux2 (
  input  [3:0] select,
  input  [3:0] line0,
  input  [3:0] line1,
  output [3:0] out
);

  wire [3:0] and_1_out, and_2_out, not_1_out;

  assign not_1_out = ~select;  // NOT_Gate not_1, 4 bits wide
  assign and_1_out = not_1_out & line0;  // AND_Gate and_1, 4 bits wide
  assign and_2_out = line1 & select;  // AND_Gate and_2, 4 bits wide
  assign out = and_1_out | and_2_out;  // OR_Gate or_1, 4 bits wide

  // Notes on the sheet:
  //   As we learned in the first lab assignment, there are "two to one" multiplexors that allow us to choose between two inputs based on a third input.
endmodule

// flip
module flipper (
  input  [3:0] in,
  output [3:0] out
);

  not not_1 (out[0], in[0]);
  not not_2 (out[1], in[1]);
  not not_3 (out[2], in[2]);
  not not_4 (out[3], in[3]);

  // Notes on the sheet:
  //   As the name suggests, this circuit is a flipper, or inverter. I will use it to flip the 4-bit inputs if needed.
  //   I don't know if the splitter was introduced in class, but it is the only way I found to split the 4-bit input
endmodule
