// Logisim project hw1q1.circ as structural Verilog: 1 circuit, main circuit main
module main (
  input  C1,
  input  C0,
  output D11,
  output D10,
  output D01,
  output D00
);

  wire not_1_out, not_2_out;

  not not_1 (not_1_out, C1);
  not not_2 (not_2_out, C0);
  and and_1 (D11, C1, C0);
  and and_2 (D10, C1, not_2_out);
  and and_3 (D01, C0, not_1_out);
  and and_4 (D00, not_1_out, not_2_out);
endmodule
