// Logisim project sm.circ as structural Verilog: 3 circuits, main circuit main
module main (
  input  \input ,
  input  clear,
  output just_saw_101
);

  wire clock_1_out;
  wire [1:0] next_1_s0_prime, register_1_q;

  next next_1 (
    .\input (\input ), .s1(register_1_q[1]), .s0(register_1_q[0]), .s1_prime(next_1_s0_prime[1]),
    .s0_prime(next_1_s0_prime[0]));
  Clock clock_1 (.out(clock_1_out));
  Register #(.width(2)) register_1 (.D(next_1_s0_prime), .en(1'b1), .Q(register_1_q), .clk(clock_1_out), .clr(clear));
  out out_1 (.s1(register_1_q[1]), .s0(register_1_q[0]), .\output (just_saw_101));
endmodule

module next (
  input  \input ,
  input  s1,
  input  s0,
  output s1_prime,
  output s0_prime
);

  wire and_1_out, and_2_out, not_1_out, not_2_out;

  not not_1 (not_1_out, s1);
  and and_1 (and_1_out, \input , not_1_out, s0);
  not not_2 (not_2_out, \input );
  and and_2 (and_2_out, not_2_out, s1);
  or or_1 (s1_prime, \input , and_1_out);
  or or_2 (s0_prime, and_1_out, and_2_out);
endmodule

module out (
  input  s1,
  input  s0,
  output \output 
);

  and and_1 (\output , s1, s0);
endmodule
