// Logisim project lab1.circ as structural Verilog: 1 circuit, main circuit main
module main (
  input  in_1,
  input  in_2,
  input  in_3,
  input  in_4,
  input  in_5,
  input  in_6,
  output out_7,
  output out_8
);

  wire and_1_out, or_1_out, or_2_out, or_3_out;

  and and_1 (and_1_out, in_1, in_2, in_3);
  or or_1 (or_1_out, in_5, in_4);
  or or_2 (or_2_out, in_4, in_6);
  or or_3 (or_3_out, in_6, in_5);
  buf or_4 (out_7, and_1_out);  // OR_Gate
  and and_2 (out_8, or_1_out, or_2_out, or_3_out);
endmodule
