// Logisim project mux4.circ as structural Verilog: 1 circuit, main circuit main
module main (
  input  select0,
  input  select1,
  input  line00,
  input  line01,
  input  line02,
  input  line03,
  output out_7
);

  wire and_1_out, and_2_out, and_3_out, and_4_out, not_1_out, not_2_out, not_3_out, not_4_out, not_5_out,
       not_6_out;

  not not_1 (not_1_out, select0);
  not not_2 (not_2_out, select1);
  not not_3 (not_3_out, line00);
  not not_4 (not_4_out, line01);
  not not_5 (not_5_out, line02);
  not not_6 (not_6_out, line03);
  and and_1 (and_1_out, not_1_out, not_2_out, line00);
  and and_2 (and_2_out, not_1_out, not_1_out, select1, select1, line01);
  and and_3 (and_3_out, select0, select0, not_2_out, not_2_out, line02);
  and and_4 (and_4_out, select0, select1, line03);
  or or_1 (out_7, and_1_out, and_2_out, and_3_out, and_4_out);
endmodule
