// Logisim project lab2.circ as structural Verilog: 3 circuits, main circuit 4bit-neg
module _4bit_neg (
  input  a3,
  input  a2,
  input  a1,
  input  a0,
  input  plus_1,
  output out3,
  output out2,
  output out1,
  output out0
);

  wire adder_1_cout, adder_2_cout, adder_3_cout, not_1_out, not_2_out, not_3_out, not_4_out;

  not not_1 (not_1_out, a3);
  not not_2 (not_2_out, a2);
  not not_3 (not_3_out, a1);
  not not_4 (not_4_out, a0);
  Adder #(.width(1)) adder_1 (.a(not_3_out), .b(adder_2_cout), .out(out1), .cout(adder_1_cout));  // open: cin
  Adder #(.width(1)) adder_2 (.a(not_4_out), .b(plus_1), .out(out0), .cout(adder_2_cout));  // open: cin
  Adder #(.width(1)) adder_3 (.a(not_2_out), .b(adder_1_cout), .out(out2), .cout(adder_3_cout));  // open: cin
  Adder #(.width(1)) adder_4 (.a(not_1_out), .b(adder_3_cout), .out(out3));  // open: cin, cout

  // Notes on the sheet:
  //   This lab was a collaboration between Keith Ng and Rahoul Juan de Kobbe
endmodule

module subtractor (
  input  a3,
  input  a2,
  input  a1,
  input  a0,
  input  b3,
  input  b2,
  input  b1,
  input  b0,
  input  plus_1,
  output out3,
  output out2,
  output out1,
  output out0
);

  wire adder_1_cout, adder_2_cout, adder_3_cout, n4bit_neg_1_out0, n4bit_neg_1_out1, n4bit_neg_1_out2,
       n4bit_neg_1_out3;

  _4bit_neg u_4bit_neg_1 (
    .a3(b3), .a2(b2), .a1(b1), .a0(b0), .plus_1(plus_1), .out3(n4bit_neg_1_out3), .out2(n4bit_neg_1_out2),
    .out1(n4bit_neg_1_out1), .out0(n4bit_neg_1_out0));
  Adder #(.width(1)) adder_1 (.a(a0), .b(n4bit_neg_1_out0), .out(out0), .cout(adder_1_cout));  // open: cin
  Adder #(.width(1)) adder_2 (.a(a1), .b(n4bit_neg_1_out1), .out(out1), .cin(adder_1_cout), .cout(adder_2_cout));
  Adder #(.width(1)) adder_3 (.a(a2), .b(n4bit_neg_1_out2), .out(out2), .cin(adder_2_cout), .cout(adder_3_cout));
  Adder #(.width(1)) adder_4 (.a(a3), .b(n4bit_neg_1_out3), .out(out3), .cin(adder_3_cout));  // open: cout
endmodule

module comparator (
  input  a3,
  input  a2,
  input  a1,
  input  a0,
  input  b3,
  input  b2,
  input  b1,
  input  b0,
  input  plus_1,
  output \output 
);

  wire and_1_out, and_2_out, not_1_out, not_2_out, not_3_out, not_4_out, subtractor_1_out0,
       subtractor_1_out1, subtractor_1_out2, subtractor_1_out3;

  not not_1 (not_1_out, subtractor_1_out3);
  subtractor subtractor_1 (
    .a3(a3), .a2(a2), .a1(a1), .a0(a0), .b3(b3), .b2(b2), .b1(b1), .b0(b0), .plus_1(plus_1),
    .out3(subtractor_1_out3), .out2(subtractor_1_out2), .out1(subtractor_1_out1), .out0(subtractor_1_out0));
  not not_2 (not_2_out, subtractor_1_out2);
  not not_3 (not_3_out, subtractor_1_out1);
  not not_4 (not_4_out, subtractor_1_out0);
  and and_1 (and_1_out, not_1_out, not_2_out);
  and and_2 (and_2_out, not_3_out, not_4_out);
  and and_3 (\output , and_1_out, and_2_out);
endmodule
