// Logisim project lab2rahoul.circ as structural Verilog
module _4bit_neg (
  input  a3,
  input  a2,
  input  a1,
  input  a0,
  input  plus_1,
  output out3,
  output out2,
  output out1,
  output out0
);

  wire half_adder_1_carry, half_adder_2_carry, half_adder_4_carry, not_1_out, not_2_out, not_3_out, not_4_out;

  not not_1 (not_1_out, a3);
  not not_2 (not_2_out, a2);
  not not_3 (not_3_out, a1);
  not not_4 (not_4_out, a0);
  Half_adder half_adder_1 (.A(not_4_out), .B(plus_1), .Carry(half_adder_1_carry), .Sum(out0));
  Half_adder half_adder_2 (.A(not_3_out), .B(half_adder_1_carry), .Carry(half_adder_2_carry), .Sum(out1));
  Half_adder half_adder_3 (.A(not_1_out), .B(half_adder_4_carry), .Sum(out3));  // open: Carry
  Half_adder half_adder_4 (.A(not_2_out), .B(half_adder_2_carry), .Carry(half_adder_4_carry), .Sum(out2));
endmodule

module Adder (
  input  A,
  input  B,
  input  Constant,
  output Carry,
  output Sum
);

  wire and_1_out, and_2_out, xor_1_out;

  xor xor_1 (xor_1_out, A, B);
  and and_1 (and_1_out, A, B);
  xor xor_2 (Sum, xor_1_out, Constant);
  and and_2 (and_2_out, xor_1_out, Constant);
  or or_1 (Carry, and_2_out, and_1_out);
endmodule

module Half_adder (
  input  A,
  input  B,
  output Carry,
  output Sum
);

  xor xor_1 (Sum, A, B);
  and and_1 (Carry, A, B);
endmodule

module subtractor (
  input  a3,
  input  a2,
  input  a1,
  input  a0,
  input  b3,
  input  b2,
  input  b1,
  input  b0,
  input  plus_1,
  output out3,
  output out2,
  output out1,
  output out0
);

  wire adder_1_carry, adder_2_carry, half_adder_1_carry, n4bit_neg_1_out0, n4bit_neg_1_out1,
       n4bit_neg_1_out2, n4bit_neg_1_out3;

  _4bit_neg u_4bit_neg_1 (
    .a3(b3), .a2(b2), .a1(b1), .a0(b0), .plus_1(plus_1), .out3(n4bit_neg_1_out3), .out2(n4bit_neg_1_out2),
    .out1(n4bit_neg_1_out1), .out0(n4bit_neg_1_out0));
  Half_adder half_adder_1 (.A(a0), .B(n4bit_neg_1_out0), .Carry(half_adder_1_carry), .Sum(out0));
  Adder adder_1 (.A(a2), .B(n4bit_neg_1_out2), .Constant(adder_2_carry), .Carry(adder_1_carry), .Sum(out2));
  Adder adder_2 (.A(a1), .B(n4bit_neg_1_out1), .Constant(half_adder_1_carry), .Carry(adder_2_carry), .Sum(out1));
  Adder adder_3 (.A(a3), .B(n4bit_neg_1_out3), .Constant(adder_1_carry), .Sum(out3));  // open: Carry
endmodule
